// Logisim project Circuit.circ as structural Verilog: 2 circuits, main circuit main
module main (
  input  [3:0] in_1,
  input  LA,
  input  CLK,
  input  EA,
  input  LC,
  input  CLK_2,
  input  EC,
  input  LB,
  input  CLK_3,
  input  EB,
  input  LD,
  input  CLK_4,
  input  ED,
  output [3:0] out_14
);

  Register A (
    .X3(in_1[3]), .X2(in_1[2]), .X1(in_1[1]), .X0(in_1[0]), .Y3(in_1[3]), .Y2(in_1[2]), .Y1(in_1[1]),
    .Y0(in_1[0]), .LOAD(LA), .Clock(CLK), .Enable(EA));  // open: Clear
  Register B (
    .X3(in_1[3]), .X2(in_1[2]), .X1(in_1[1]), .X0(in_1[0]), .Y3(in_1[3]), .Y2(in_1[2]), .Y1(in_1[1]),
    .Y0(in_1[0]), .LOAD(LB), .Clock(CLK_3), .Enable(EB));  // open: Clear
  Register C (
    .X3(in_1[3]), .X2(in_1[2]), .X1(in_1[1]), .X0(in_1[0]), .Y3(in_1[3]), .Y2(in_1[2]), .Y1(in_1[1]),
    .Y0(in_1[0]), .LOAD(LC), .Clock(CLK_2), .Enable(EC));  // open: Clear
  Register D (
    .X3(in_1[3]), .X2(in_1[2]), .X1(in_1[1]), .X0(in_1[0]), .Y3(in_1[3]), .Y2(in_1[2]), .Y1(in_1[1]),
    .Y0(in_1[0]), .LOAD(LD), .Clock(CLK_4), .Enable(ED));  // open: Clear

  assign out_14 = in_1;

  // Notes on the sheet:
  //   1607021
endmodule

module Register (
  input  X3,
  input  X2,
  input  X1,
  input  X0,
  input  LOAD,
  input  Clear,
  input  Clock,
  input  Enable,
  output Y3,
  output Y2,
  output Y1,
  output Y0
);

  wire and_1_out, and_2_out, and_3_out, and_4_out, and_5_out, and_6_out, and_7_out, and_8_out, D0_q, D1_q,
       D2_q, D3_q, not_1_out, or_1_out, or_2_out, or_3_out, or_4_out;

  assign Y3 = Enable ? D3_q : 1'bz;  // Controlled_Buffer controlled_buffer_1
  and and_1 (and_1_out, D3_q, not_1_out);
  or or_1 (or_1_out, and_1_out, and_2_out);
  D_Flip_Flop D3 (.clk(Clock), .D(or_1_out), .Q(D3_q), .reset(Clear));  // open: Qn, preset, en
  and and_2 (and_2_out, X3, LOAD);
  and and_3 (and_3_out, D2_q, not_1_out);
  assign Y2 = Enable ? D2_q : 1'bz;  // Controlled_Buffer controlled_buffer_2
  and and_4 (and_4_out, X2, LOAD);
  or or_2 (or_2_out, and_3_out, and_4_out);
  D_Flip_Flop D2 (.clk(Clock), .D(or_2_out), .Q(D2_q), .reset(Clear));  // open: Qn, preset, en
  assign Y1 = Enable ? D1_q : 1'bz;  // Controlled_Buffer controlled_buffer_3
  and and_5 (and_5_out, D1_q, not_1_out);
  or or_3 (or_3_out, and_5_out, and_6_out);
  D_Flip_Flop D1 (.clk(Clock), .D(or_3_out), .Q(D1_q), .reset(Clear));  // open: Qn, preset, en
  and and_6 (and_6_out, X1, LOAD);
  assign Y0 = Enable ? D0_q : 1'bz;  // Controlled_Buffer controlled_buffer_4
  and and_7 (and_7_out, D0_q, not_1_out);
  or or_4 (or_4_out, and_7_out, and_8_out);
  D_Flip_Flop D0 (.clk(Clock), .D(or_4_out), .Q(D0_q), .reset(Clear));  // open: Qn, preset, en
  not not_1 (not_1_out, LOAD);
  and and_8 (and_8_out, X0, LOAD);

  // Notes on the sheet:
  //   1607021
endmodule
