// Logisim project Circuit.circ as structural Verilog: 3 circuits, main circuit main
module main (
  input  S1,
  input  S0,
  input  Cin,
  input  A1,
  input  B1,
  input  A2,
  input  B2,
  input  A3,
  input  B3,
  input  A4,
  input  B4,
  input  A5,
  input  B5,
  input  A6,
  input  B6,
  input  A7,
  input  B7,
  input  A8,
  input  B8,
  output F1,
  output F2,
  output F3,
  output F4,
  output F5,
  output F6,
  output F7,
  output F8
);

  wire fa_1_c, fa_2_c, fa_3_c, fa_4_c, fa_5_c, fa_6_c, fa_7_c, one_zerocircuit_1_y, one_zerocircuit_2_y,
       one_zerocircuit_3_y, one_zerocircuit_4_y, one_zerocircuit_5_y, one_zerocircuit_6_y,
       one_zerocircuit_7_y, one_zerocircuit_8_y;

  One_ZeroCircuit one_zerocircuit_1 (.B(B1), .S0(S0), .S1(S1), .Y(one_zerocircuit_1_y));
  One_ZeroCircuit one_zerocircuit_2 (.B(B2), .S0(S0), .S1(S1), .Y(one_zerocircuit_2_y));
  One_ZeroCircuit one_zerocircuit_3 (.B(B3), .S0(S0), .S1(S1), .Y(one_zerocircuit_3_y));
  One_ZeroCircuit one_zerocircuit_4 (.B(B4), .S0(S0), .S1(S1), .Y(one_zerocircuit_4_y));
  One_ZeroCircuit one_zerocircuit_5 (.B(B5), .S0(S0), .S1(S1), .Y(one_zerocircuit_5_y));
  One_ZeroCircuit one_zerocircuit_6 (.B(B6), .S0(S0), .S1(S1), .Y(one_zerocircuit_6_y));
  One_ZeroCircuit one_zerocircuit_7 (.B(B7), .S0(S0), .S1(S1), .Y(one_zerocircuit_7_y));
  One_ZeroCircuit one_zerocircuit_8 (.B(B8), .S0(S0), .S1(S1), .Y(one_zerocircuit_8_y));
  FA fa_1 (.X(A1), .Y(one_zerocircuit_1_y), .Z(Cin), .S(F1), .C(fa_1_c));
  FA fa_2 (.X(A2), .Y(one_zerocircuit_2_y), .Z(fa_1_c), .S(F2), .C(fa_2_c));
  FA fa_3 (.X(A3), .Y(one_zerocircuit_3_y), .Z(fa_2_c), .S(F3), .C(fa_3_c));
  FA fa_4 (.X(A4), .Y(one_zerocircuit_4_y), .Z(fa_3_c), .S(F4), .C(fa_4_c));
  FA fa_5 (.X(A5), .Y(one_zerocircuit_5_y), .Z(fa_4_c), .S(F5), .C(fa_5_c));
  FA fa_6 (.X(A6), .Y(one_zerocircuit_6_y), .Z(fa_5_c), .S(F6), .C(fa_6_c));
  FA fa_7 (.X(A7), .Y(one_zerocircuit_7_y), .Z(fa_6_c), .S(F7), .C(fa_7_c));
  FA fa_8 (.X(A8), .Y(one_zerocircuit_8_y), .Z(fa_7_c), .S(F8));  // open: C

  // Notes on the sheet:
  //   1607021
  //   A = 2
  //   B = 1
  //   Logic Diagram of Arithmetic Circuit
endmodule

module FA (
  input  X,
  input  Y,
  input  Z,
  output S,
  output C
);

  wire and_1_out, and_2_out, xor_1_out;

  xor xor_1 (xor_1_out, X, Y);
  and and_1 (and_1_out, X, Y);
  xor xor_2 (S, xor_1_out, Z);
  and and_2 (and_2_out, xor_1_out, Z);
  or or_1 (C, and_2_out, and_1_out);

  // Notes on the sheet:
  //   1607021
  //   Implementation of FA
endmodule

// 0/1
module One_ZeroCircuit (
  input  B,
  input  S0,
  input  S1,
  output Y
);

  wire and_1_out, and_2_out, not_1_out;

  not not_1 (not_1_out, B);
  and and_1 (and_1_out, B, S0);
  and and_2 (and_2_out, not_1_out, S1);
  or or_1 (Y, and_1_out, and_2_out);

  // Notes on the sheet:
  //   1607021
  //   Implementation of One/Zero Circuit
endmodule
