// Logisim project Circuit.circ as structural Verilog: 3 circuits, main circuit main
module main (
  input  Cin,
  input  S2,
  input  S1,
  input  S0,
  input  A1,
  input  B1,
  input  A2,
  input  B2,
  input  A3,
  input  B3,
  input  A4,
  input  B4,
  output F1,
  output F2,
  output F3,
  output F4,
  output Cout
);

  wire and_1_out, and_2_out, and_3_out, and_4_out, and_5_out, and_6_out, and_7_out, and_8_out, and_9_out,
       and_10_out, and_11_out, fa_1_c, fa_2_c, fa_3_c, not_1_out, not_2_out, not_3_out, not_4_out, not_5_out,
       not_6_out, not_7_out, one_zerocircuit_1_y, one_zerocircuit_2_y, one_zerocircuit_3_y,
       one_zerocircuit_4_y, or_1_out, or_2_out, or_3_out, or_4_out;

  not not_1 (not_1_out, S2);
  not not_2 (not_2_out, S0);
  not not_3 (not_3_out, B1);
  and and_1 (and_1_out, not_2_out, S1, S2);
  One_ZeroCircuit one_zerocircuit_1 (.B(B1), .S0(S0), .S1(S1), .Y(one_zerocircuit_1_y));
  not not_4 (not_4_out, B2);
  One_ZeroCircuit one_zerocircuit_2 (.B(B2), .S0(S0), .S1(S1), .Y(one_zerocircuit_2_y));
  not not_5 (not_5_out, B3);
  One_ZeroCircuit one_zerocircuit_3 (.B(B3), .S0(S0), .S1(S1), .Y(one_zerocircuit_3_y));
  not not_6 (not_6_out, B4);
  One_ZeroCircuit one_zerocircuit_4 (.B(B4), .S0(S0), .S1(S1), .Y(one_zerocircuit_4_y));
  not not_7 (not_7_out, S1);
  and and_2 (and_2_out, not_2_out, not_7_out, S2);
  and and_3 (and_3_out, and_2_out, B1);
  and and_4 (and_4_out, and_1_out, not_3_out);
  and and_5 (and_5_out, and_2_out, B2);
  and and_6 (and_6_out, and_1_out, not_4_out);
  and and_7 (and_7_out, and_2_out, B3);
  and and_8 (and_8_out, and_1_out, not_5_out);
  and and_9 (and_9_out, and_2_out, B4);
  and and_10 (and_10_out, and_1_out, not_6_out);
  and and_11 (and_11_out, not_1_out, Cin);
  or or_1 (or_1_out, and_3_out, and_4_out, A1);
  or or_2 (or_2_out, and_5_out, and_6_out, A2);
  or or_3 (or_3_out, and_7_out, and_8_out, A3);
  or or_4 (or_4_out, and_9_out, and_10_out, A4);
  FA fa_1 (.X(or_1_out), .Y(one_zerocircuit_1_y), .Z(and_11_out), .S(F1), .C(fa_1_c));
  FA fa_2 (.X(or_2_out), .Y(one_zerocircuit_2_y), .Z(fa_1_c), .S(F2), .C(fa_2_c));
  FA fa_3 (.X(or_3_out), .Y(one_zerocircuit_3_y), .Z(fa_2_c), .S(F3), .C(fa_3_c));
  FA fa_4 (.X(or_4_out), .Y(one_zerocircuit_4_y), .Z(fa_3_c), .S(F4), .C(Cout));

  // Notes on the sheet:
  //   1607021
endmodule

module FA (
  input  X,
  input  Y,
  input  Z,
  output S,
  output C
);

  wire and_1_out, and_2_out, xor_1_out;

  xor xor_1 (xor_1_out, X, Y);
  and and_1 (and_1_out, X, Y);
  xor xor_2 (S, xor_1_out, Z);
  and and_2 (and_2_out, xor_1_out, Z);
  or or_1 (C, and_2_out, and_1_out);

  // Notes on the sheet:
  //   1607021
  //   Implementation of FA
endmodule

// 0/1
module One_ZeroCircuit (
  input  B,
  input  S0,
  input  S1,
  output Y
);

  wire and_1_out, and_2_out, not_1_out;

  not not_1 (not_1_out, B);
  and and_1 (and_1_out, B, S0);
  and and_2 (and_2_out, not_1_out, S1);
  or or_1 (Y, and_1_out, and_2_out);

  // Notes on the sheet:
  //   1607021
  //   Implementation of One/Zero Circuit
endmodule
